# Fritzing sketch Sketch-cables (saved by Fritzing 0.9.3b)

parts:
  U1 = NodeMCU V1.0
  Componente1 = RFID-RC522-v2

nets:
  N1: U1.D1, Componente1.RST
  N2: U1.D2, Componente1.SDA
  3V3: U1.3V3, Componente1.3.3V
  GND: U1.GND, Componente1.GND
  N3: U1.D5, Componente1.SCK
  N4: U1.D6, Componente1.MISO
  N5: U1.D7, Componente1.MOSI

custom parts:
  NodeMCU V1.0: ESP8266 based NodeMCU
  RFID-RC522-v2: A simple China made RFID-RC522 Reader; do check the pin labels, as this is a MFRC522 based clone.
