# Fritzing sketch Sketch-SD-RC522 (saved by Fritzing 0.9.3b)

parts:
  U1 = NodeMCU V1.0
  Componente1 = RFID-RC522-v2
  Componente2 = MicroSD Card Module

nets:
  N1: U1.D1, Componente1.RST
  N2: U1.D2, Componente1.SDA
  3V3: U1.3V3, Componente1.3.3V, Componente2.VCC
  GND: U1.GND, Componente1.GND, Componente2.GND
  N3: U1.D5, Componente1.SCK
  N4: U1.D6, Componente1.MISO
  N5: U1.D7, Componente1.MOSI
  N6: U1.RX, Componente2.MOSI
  N7: U1.TX, Componente2.CS
  N8: U1.CLK, Componente2.SCK
  N9: U1.SD0, Componente2.MISO

custom parts:
  NodeMCU V1.0: ESP8266 based NodeMCU
  RFID-RC522-v2: A simple China made RFID-RC522 Reader; do check the pin labels, as this is a MFRC522 based clone.
