# Fritzing sketch Sketch-sd (saved by Fritzing 0.9.3b)

parts:
  U1 = NodeMCU V1.0
  Componente1 = MicroSD Card Module

nets:
  3V3: U1.3V3, Componente1.VCC
  GND: U1.GND, Componente1.GND
  N1: U1.D5, Componente1.SCK
  N2: U1.D6, Componente1.MISO
  N3: U1.D7, Componente1.MOSI
  N4: U1.D8, Componente1.CS

custom parts:
  NodeMCU V1.0: ESP8266 based NodeMCU
