# Fritzing sketch SKETCH1 (saved by Fritzing 0.9.3b)
circuit board: 8.46667cm x 5.64444cm

parts:
  U1 = NodeMCU V1.0
  J1 = Basic Servo
  hc-sr1 = hc-sr04
  LED1 = LED - 5mm [color="Red (633nm)" package="5 mm [THT]"]
  LED2 = LED - 5mm [color="Green (560nm)" package="5 mm [THT]"]
  S1 = SWITCH-MOMENTARY-2 [package=tactile-pth-12mm]
  Componente1 = RDM6300-ANT
  R1 = Resistor [tolerance=±5% resistance=10k package="0603 [SMD]"]
  125_kHz_RFID_module1 = RDM6300

nets:
  N1: U1.D1, LED1.anode
  N2: U1.D2, LED2.anode
  N3: U1.D4, R1.Pin_0
  GND: U1.GND, J1.gnd, hc-sr1.GND, LED2.cathode, 125_kHz_RFID_module1.GND#60
  N4: U1.D5, hc-sr1.Echo
  N5: U1.D6, hc-sr1.Trig
  N6: U1.D7, J1.pulse
  N7: U1.RX, 125_kHz_RFID_module1.TX, 125_kHz_RFID_module1.GND#66, 125_kHz_RFID_module1.GND#67
  N8: U1.3V3, S1.2
  VCC: U1.Vin, J1.vcc, hc-sr1.VCC, 125_kHz_RFID_module1.+5V
  N9: Componente1.ANT1, 125_kHz_RFID_module1.ANT1
  N10: Componente1.ANT2, 125_kHz_RFID_module1.ANT2

custom parts:
  NodeMCU V1.0: ESP8266 based NodeMCU
  RDM6300-ANT: Antenna
  RDM6300: 125 kHz RFID module (serial interface)
